// Logisim project 4 BIT ADD SUBTRACT.circ as structural Verilog: 1 circuit, main circuit main
module main (
  input  B0,
  input  B1,
  input  B2,
  input  B3,
  input  Cin,
  input  A0,
  input  A1,
  input  A2,
  input  A3,
  output S0,
  output S1,
  output S2,
  output S3,
  output Cout
);

  wire and_1_out, and_2_out, and_3_out, and_4_out, and_5_out, and_6_out, and_7_out, and_8_out, xor_1_out,
       xor_2_out, xor_4_out, xor_5_out, xor_6_out, xor_8_out, xor_9_out, xor_10_out, xor_12_out, xor_13_out,
       xor_14_out;

  xor xor_1 (xor_1_out, B0, Cin);
  xor xor_2 (xor_2_out, xor_1_out, A0);
  xor xor_3 (S0, xor_2_out, Cin);
  and and_1 (and_1_out, Cin, xor_2_out);
  and and_2 (and_2_out, A0, xor_1_out);
  xor xor_4 (xor_4_out, and_1_out, and_2_out);
  xor xor_5 (xor_5_out, B1, Cin);
  xor xor_6 (xor_6_out, xor_5_out, A1);
  xor xor_7 (S1, xor_6_out, xor_4_out);
  and and_3 (and_3_out, xor_4_out, xor_6_out);
  and and_4 (and_4_out, A1, xor_5_out);
  xor xor_8 (xor_8_out, and_3_out, and_4_out);
  xor xor_9 (xor_9_out, B2, Cin);
  xor xor_10 (xor_10_out, xor_9_out, A2);
  xor xor_11 (S2, xor_10_out, xor_8_out);
  and and_5 (and_5_out, xor_8_out, xor_10_out);
  and and_6 (and_6_out, A2, xor_9_out);
  xor xor_12 (xor_12_out, B3, Cin);
  xor xor_13 (xor_13_out, and_5_out, and_6_out);
  xor xor_14 (xor_14_out, xor_12_out, A3);
  xor xor_15 (S3, xor_14_out, xor_13_out);
  and and_7 (and_7_out, xor_13_out, xor_14_out);
  and and_8 (and_8_out, A3, xor_12_out);
  xor xor_16 (Cout, and_7_out, and_8_out);

  // Notes on the sheet:
  //   SUM 
  //   ( Cin = 0 )
  //   DIFFERENCE
  //   ( Cin = 1 )
  //   A3 A2 A1 A0 -  B3 B2 B1 B0 =  S3 S2 S1 S0
  //   A3 A2 A1 A0 + B3 B2 B1 B0 = Cout S3 S2 S1 S0
  //   Prepared by: Aisyah (1919658)
endmodule
